# Fritzing sketch Mega&ES_W5100 (saved by Fritzing 0.9.3b)
breadboards: 1

parts:
  Part1 = Arduino Mega ADK (Rev3)
  Part2 = Arduino Ethernet Shield (Rev3)
  U1 = 4-Channel 5v Relay Shield [package=relay-4ch5v10a]
  part = Water Level Sensor
  J1 = Piezo Speaker
  PIR2 = PIR sensor
  BMP180_Breakout1 = Barometric Pressure Sensor - BMP180 Breakout (GY-68)
  MQ-5_Breakout1 = Gas Sensor Breakout Board
  R1 = Resistor [tolerance=±5% resistance=10k package=THT]
  LED1 = LEDs [package=led10mm]
  RHT1 = Humidity and Temperature Sensor RHT03
  DHT1 = DHT11 Humitidy and Temperature Sensor
  R2 = Resistor [tolerance=±5% resistance=10k package=THT]
  SP2 = SPEAKER [package=pcb_mount_speaker]

nets:
  N1: Part1.A0, MQ-5_Breakout1.AOUT
  N2: Part1.A1, Part2.A1, DHT1.DATA
  N3: Part1.A2, RHT1.Data-signal, R2.Pin_1
  N4: Part1.A3, Part2.A3
  N5: Part1.A4, Part2.A4/SDA
  N6: Part1.A5, Part2.A5/SCL
  N7: Part1.D21/SCL, BMP180_Breakout1.SDA
  N8: Part1.D20/SDA, BMP180_Breakout1.SCL
  N9: Part1.AREF, Part2.AREF
  N10: Part1.D13_PWM, Part2.SPI/D13
  N11: Part1.D12_PWM, Part2.SPI/D12
  N12: Part1.D11_PWM, Part2.PWM_D11
  N13: Part1.D10_PWM, Part2.ETH_CS
  N14: Part1.D9_PWM, Part2.PWM_D9
  N15: Part1.D8_PWM, Part2.D8
  N16: Part1.IOREF#302, Part2.N/A
  VCC: Part1.IOREF#303, Part1.5V, Part2.IOREF, U1.VCC, part.VCC, J1.pin1, PIR2.VDD, RHT1.Vcc, DHT1.VDD, R2.Pin_0
  N17: Part1.RESET, Part2.RESET
  3V3: Part1.3V3, Part2.3V3, BMP180_Breakout1.VCC, MQ-5_Breakout1.5V
  GND: Part1.GND, Part2.GND, U1.GND, part.GND, PIR2.GND, BMP180_Breakout1.GND, MQ-5_Breakout1.GND, LED1.C, RHT1.GND_2, DHT1.GND
  VIN: Part1.VIN, Part2.VIN
  N18: Part1.D0/RX0, Part2.RX/D0
  N19: Part1.D1/TX0, Part2.TX/D1
  N20: Part1.D2_PWM, Part2.D2
  N21: Part1.D3_PWM, Part2.PWM_D3
  N22: Part1.D4_PWM, Part2.SDCS
  N23: Part1.D5_PWM, Part2.PWM_D5
  N24: Part1.D6_PWM, Part2.PWM_D6
  N25: Part1.D7_PWM, Part2.D7
  N26: Part1.D22, U1.IN1
  N27: Part1.D23, U1.IN2
  N28: Part1.D24, U1.IN3
  N29: Part1.D25, U1.IN4
  N30: Part1.D26, part.SIG
  N31: Part1.D46, J1.pin2
  N32: Part1.D50/MISO, PIR2.SIG, R1.Pin_0
  N33: U1.K1-In, SP2.+
  N34: U1.K1-Off, SP2.-
  N35: R1.Pin_1, LED1.A

custom parts:
  4-Channel 5v Relay Shield: 4 Channel 5v Relay Shield w. 2x SPD-06VDC-SD-C
  Water Level Sensor: A water level sensor. This sensor operates at 3V to 5V. The Sig (signal) pin outputs an analogue signal that is in proportion to the amount of water in contact with the sensor.
  Gas Sensor Breakout Board: Gas sensor breakout board. Input voltage is 5V. Sensor output is available in analog and digital.
  DHT11 Humitidy and Temperature Sensor: DHT11 Humidity and Temperature Sensor
